# Fritzing sketch LEDStrip (saved by Fritzing 0.9.4)
circuit board: 9.46116cm x 6.43019cm
breadboards: 2

parts:
  12V_Input = Power plug
  220µF = Electrolytic Capacitor [capacitance=220µF voltage=20V package="100 mil [THT, electrolytic]"]
  470µF = Electrolytic Capacitor [capacitance=470µF voltage=20V package="100 mil [THT, electrolytic]"]
  M1 = ESP32-S2-DevKitC-1 [part_number=ESP32-S2-DevKitC-1]
  LED_Strip_Addressable = female pin header, 3 pins [form="♀ (female)"]
  LCD = female pin header, 4 pins [form="♀ (female)"]
  5v = female pin header, 2 pins [form="♀ (female)"]
  Schottky = Rectifier Diode [package="Melf DO-213 AA [SMD]"]
  33uH = Inductors [package=cr54]
  Mic = female pin header, 5 pins [form="♀ (female)"]
  Schottky_2 = Rectifier Diode [package="Melf DO-213 AA [SMD]"]
  220µF_2 = Electrolytic Capacitor [capacitance=220µF package="100 mil [THT, electrolytic]"]
  220µF_3 = Electrolytic Capacitor [capacitance=220µF package="100 mil [THT, electrolytic]"]
  470µF_2 = Electrolytic Capacitor [capacitance=470µF package="100 mil [THT, electrolytic]"]
  33uH_2 = Inductors [package=cr54]
  3_3V = female pin header, 2 pins [form="♀ (female)"]
  12V = female pin header, 2 pins [form="♀ (female)"]
  MSGEQ1 = MSGEQ7 [chip_label=IC package="DIP (Dual Inline) [THT]"]
  LM2596_2 = LM2596 [package=q5-dd_spx29300]
  33pF = Capacitor [package=0603-cap]
  100nF = Capacitor [package=0603-cap]
  10nF = Capacitor [package=0603-cap]
  100nF_2 = Capacitor [package=0603-cap]
  LED_Strip = female pin header, 4 pins [form="♀ (female)"]
  LED_Matrix = female pin header, 5 pins [form="♀ (female)"]
  Pot_BK = female pin header, 3 pins [form="♀ (female)"]
  Gain_Pot = female pin header, 3 pins [form="♀ (female)"]
  Backlight = JUMPER-3 [package=sj_3_paste2_3]
  Button = female pin header, 4 pins [form="♀ (female)"]
  LM2596_1 = LM2596 [package=q5-dd_spx29300]
  Gain = JUMPER-3 [package=sj_3_paste2_3]
  220Ω = Resistor [tolerance=±5% resistance=220 package="0603 [SMD]"]
  2kΩ = Resistor [tolerance=±1% resistance=2k package="0603 [SMD]"]
  1kΩ = Resistor [tolerance=±1% resistance=1k package="0603 [SMD]"]
  200kΩ = Resistor [tolerance=±1% resistance=200k package="0603 [SMD]"]
  20kΩ = Resistor [tolerance=±1% resistance=20k package="0603 [SMD]"]
  330Ω = Resistor [tolerance=±1% resistance=330 package="0603 [SMD]"]
  MOSFET_G = Basic FET N-Channel [package="D2Pak [SMD]"]
  MOSFET_R = Basic FET N-Channel [package="D2Pak [SMD]"]
  MOSFET_B = Basic FET N-Channel [package="D2Pak [SMD]"]
  220µF_4 = Tantalum Capacitor [capacitance=220µF voltage=20V package="D 7343 [SMD, tantalum]"]

nets:
  GND: 12V_Input.GND, 220µF.-, 470µF.-, M1.pin_22, M1.pin_23, M1.pin_24, M1.pin_44, LED_Strip_Addressable.pin3, 5v.pin1, Schottky.anode, Mic.pin5, Schottky_2.anode, 220µF_2.-, 220µF_3.-, 470µF_2.-, 3_3V.pin1, 12V.pin1, MSGEQ1.VSS, LM2596_2.GND, LM2596_2.On/Off, 33pF.2, 100nF.1, 100nF_2.1, LED_Matrix.pin4, Pot_BK.pin1, Gain_Pot.pin1, Backlight.1, LM2596_1.GND, LM2596_1.On/Off, Gain.1, 220Ω.Pin_0, 1kΩ.Pin_1, MOSFET_G.source, MOSFET_R.source, MOSFET_B.source, 220µF_4.-
  VIN: 12V_Input.VCC, 220µF.+, 470µF.+, 220µF_2.+, 470µF_2.+, 12V.pin2, LM2596_2.VIN, LED_Strip.pin4, LM2596_1.VIN
  N1: M1.pin_1, M1.pin_2, LCD.pin1, Mic.pin4, 3_3V.pin2, Pot_BK.pin3, Gain_Pot.pin3, Backlight.3, Button.pin2, Button.pin3, Gain.3
  N2: M1.pin_4, Button.pin1, 1kΩ.Pin_0
  N3: M1.pin_5, MSGEQ1.GND
  N4: M1.pin_11, LCD.pin3
  N5: M1.pin_15, LCD.pin2
  N6: M1.pin_21, 33uH.2, MSGEQ1.VDD, 100nF_2.2, LM2596_1.Feedback, 200kΩ.Pin_0, 220µF_4.+
  N7: M1.pin_28, LED_Matrix.pin2
  N8: M1.pin_29, LED_Matrix.pin1
  N9: M1.pin_30, LED_Matrix.pin3
  N10: M1.pin_36, MOSFET_B.Gate
  N11: M1.pin_37, MOSFET_R.Gate
  N12: M1.pin_38, MOSFET_G.Gate
  N13: M1.pin_39, 330Ω.Pin_0
  N14: M1.pin_40, MSGEQ1.STROBE
  N15: M1.pin_41, MSGEQ1.OUT
  N16: LED_Strip_Addressable.pin1, 5v.pin2, 220µF_3.+, 33uH_2.2, LM2596_2.Feedback, LED_Matrix.pin5
  N17: LED_Strip_Addressable.pin2, 330Ω.Pin_1
  N18: Schottky.cathode, 33uH.1, LM2596_1.OUT
  N19: Mic.pin2, 20kΩ.Pin_1
  N20: Mic.pin3, Gain_Pot.pin2, Gain.2
  N21: Schottky_2.cathode, 33uH_2.1, LM2596_2.OUT
  N22: MSGEQ1.IN, 10nF.1
  N23: MSGEQ1.pin6, 100nF.2
  N24: MSGEQ1.CKIN, 33pF.1, 200kΩ.Pin_1
  N25: 10nF.2, 2kΩ.Pin_0
  N26: LED_Strip.pin1, MOSFET_B.drain
  N27: LED_Strip.pin2, MOSFET_R.drain
  N28: LED_Strip.pin3, MOSFET_G.drain
  N29: Pot_BK.pin2, Backlight.2
  N30: Button.pin4, 220Ω.Pin_1
  N31: 2kΩ.Pin_1, 20kΩ.Pin_0

notes:
  Note that the ESP32 board below is ESP32 S2. I'm actually using ESP32 S3 so I'm keeping the pin LOCATION constant and ignoring the pin NUMBERS for the bottom rail which differ between S2 and S3.

custom parts:
  ESP32-S2-DevKitC-1: ESP32-S2-DevKitC-1 is an entry-level development board based on ESP32-S2-SOLO (on-board PCB antenna). It is based on the ESP32 microcontroller that boasts Wifi, Bluetooth, Ethernet and Low Power support all in a single chip. (vanepp) Feb 2022: converted to ESP32-S2-DevKitC-1. This module is 44pins long (2x22) and 11 pins width.
  MSGEQ7: A DIP stand-in part for whatever IC you want. With 8 pins on a 300mil dual inline package (DIP) footprint.
  LM2596: LM2596 SIMPLE SWITCHER® Power Converter 150-kHz 3-A Step-Down Voltage Regulator
